// Logisim project branch-comp.circ as structural Verilog: 1 circuit, main circuit branch_comp
module branch_comp (
  input  [31:0] BrData1,
  input  [31:0] BrData2,
  input  BrUn,
  output BrEq,
  output BrLt
);

  wire BrEq_sign, BrEq_unsign, BrLt_sign, BrLt_unsign, comparator_1_eq, comparator_1_lt, comparator_2_eq,
       comparator_2_lt, not_1_out;

  Comparator #(.width(32)) comparator_1 (
    .a(BrData1), .b(BrData2), .eq(comparator_1_eq), .lt(comparator_1_lt));  // open: gt
  not not_1 (not_1_out, BrUn);
  Comparator #(.mode("unsigned"), .width(32)) comparator_2 (
    .a(BrData1), .b(BrData2), .eq(comparator_2_eq), .lt(comparator_2_lt));  // open: gt
  and and_1 (BrEq_sign, comparator_1_eq, not_1_out);
  and and_2 (BrLt_sign, comparator_1_lt, not_1_out);
  and and_3 (BrEq_unsign, comparator_2_eq, BrUn);
  and and_4 (BrLt_unsign, comparator_2_lt, BrUn);
  or or_1 (BrEq, BrEq_sign, BrEq_unsign);
  or or_2 (BrLt, BrLt_sign, BrLt_unsign);

  // Notes on the sheet:
  //   INPUTS to your circuit
  //   DON'T CHANGE THE LOCATIONS OF THE INPUTS AND OUTPUTS!
  //   OUTPUT from your circuit
endmodule
