// Logisim project control-logic.circ as structural Verilog: 1 circuit, main circuit control_logic
module control_logic (
  input  [31:0] Instruction,
  input  BrEq,
  input  BrLt,
  output PCSel,
  output RegWEn,
  output [2:0] ImmSel,
  output BrUn,
  output ASel,
  output BSel,
  output [3:0] ALUSel,
  output MemWEn,
  output [1:0] WBSel
);

  wire and_1_out, and_2_out, and_7_out, and_20_out, and_37_out, and_38_out, and_39_out, and_40_out,
       and_41_out, and_42_out, comparator_1_eq, comparator_2_eq, comparator_3_eq, comparator_4_eq,
       comparator_5_eq, comparator_6_eq, comparator_7_eq, comparator_8_eq, comparator_9_eq, comparator_10_eq,
       comparator_10_gt, comparator_11_eq, comparator_11_gt, comparator_12_eq, comparator_12_gt,
       comparator_13_eq, comparator_13_gt, comparator_14_eq, comparator_15_eq, comparator_16_eq,
       comparator_17_eq, comparator_18_eq, comparator_19_eq, comparator_20_eq, comparator_21_eq,
       comparator_22_eq, comparator_23_eq, comparator_24_eq, comparator_25_eq, comparator_26_eq,
       comparator_26_gt, comparator_27_eq, comparator_28_eq, comparator_29_eq, comparator_30_eq,
       comparator_31_eq, comparator_32_eq, comparator_33_eq, comparator_34_eq, comparator_35_eq,
       comparator_36_eq, comparator_37_eq, is_add, is_addi, is_and, is_andi, is_auipc, is_beq, is_bge,
       is_bgeu, is_blt, is_bltu, is_bne, is_jal, is_jalr, is_lb, is_lh, is_lui, is_lw, is_mul, is_mulh,
       is_mulhu, is_or, is_ori, is_sb, is_sh, is_sll, is_slli, is_slt, is_slti, is_sra, is_srai, is_srl,
       is_srli, is_sub, is_sw, is_xor, is_xori, not_1_out, not_2_out, not_3_out;
  wire [5:0] ROMInput;
  wire [15:14] rom_1_data;

  Comparator #(.width(7)) comparator_1 (.a(Instruction[6:0]), .b(7'b0110011), .eq(comparator_1_eq));  // open: gt, lt
  Comparator #(.mode("unsigned"), .width(3)) comparator_2 (
    .a(Instruction[14:12]), .b(3'b000), .eq(comparator_2_eq));  // open: gt, lt
  Comparator #(.width(3)) comparator_3 (.a(Instruction[14:12]), .b(3'b001), .eq(comparator_3_eq));  // open: gt, lt
  Comparator #(.width(3)) comparator_4 (.a(Instruction[14:12]), .b(3'b011), .eq(comparator_4_eq));  // open: gt, lt
  Comparator #(.width(3)) comparator_5 (.a(Instruction[14:12]), .b(3'b010), .eq(comparator_5_eq));  // open: gt, lt
  Comparator #(.width(3)) comparator_6 (.a(Instruction[14:12]), .b(3'b100), .eq(comparator_6_eq));  // open: gt, lt
  Comparator #(.width(3)) comparator_7 (.a(Instruction[14:12]), .b(3'b110), .eq(comparator_7_eq));  // open: gt, lt
  Comparator #(.width(3)) comparator_8 (.a(Instruction[14:12]), .b(3'b101), .eq(comparator_8_eq));  // open: gt, lt
  Comparator #(.width(3)) comparator_9 (.a(Instruction[14:12]), .b(3'b111), .eq(comparator_9_eq));  // open: gt, lt
  ROM #(.addrWidth(6), .dataWidth(16)) rom_1 (
    .addr(ROMInput), .data({rom_1_data, WBSel, MemWEn, ALUSel, BSel, ASel, BrUn, ImmSel, RegWEn}));
  and and_1 (and_1_out, comparator_2_eq, comparator_1_eq);
  Comparator #(.width(7)) comparator_10 (
    .a(Instruction[31:25]), .b({7{1'b0}}), .gt(comparator_10_gt), .eq(comparator_10_eq));  // open: lt
  and and_2 (and_2_out, comparator_3_eq, comparator_1_eq);
  and and_3 (is_mulhu, comparator_4_eq, comparator_1_eq);
  and and_4 (is_slt, comparator_5_eq, comparator_1_eq);
  and and_5 (is_xor, comparator_6_eq, comparator_1_eq);
  and and_6 (is_or, comparator_7_eq, comparator_1_eq);
  and and_7 (and_7_out, comparator_8_eq, comparator_1_eq);
  and and_8 (is_and, comparator_9_eq, comparator_1_eq);
  Comparator #(.width(7)) comparator_11 (
    .a(Instruction[31:25]), .b({7{1'b0}}), .gt(comparator_11_gt), .eq(comparator_11_eq));  // open: lt
  Comparator #(.width(7)) comparator_12 (
    .a(Instruction[31:25]), .b({7{1'b0}}), .gt(comparator_12_gt), .eq(comparator_12_eq));  // open: lt
  Comparator #(.width(7)) comparator_13 (
    .a(Instruction[31:25]), .b(7'b0000001), .gt(comparator_13_gt), .eq(comparator_13_eq));  // open: lt
  and and_9 (is_sll, and_2_out, comparator_11_eq);
  and and_10 (is_mulh, comparator_11_gt, and_2_out);
  and and_11 (is_srl, and_7_out, comparator_12_eq);
  and and_12 (is_sra, and_7_out, comparator_12_gt);
  and and_13 (is_add, and_1_out, comparator_10_eq);
  and and_14 (is_mul, comparator_10_gt, comparator_13_eq);
  and and_15 (is_sub, comparator_10_gt, comparator_13_gt);
  Comparator #(.width(7)) comparator_14 (.a(Instruction[6:0]), .b(7'b0000011), .eq(comparator_14_eq));  // open: gt, lt
  Comparator #(.width(7)) comparator_15 (.a(Instruction[6:0]), .b(7'b0010011), .eq(comparator_15_eq));  // open: gt, lt
  Comparator #(.width(3)) comparator_16 (.a(Instruction[14:12]), .b(3'b000), .eq(comparator_16_eq));  // open: gt, lt
  Comparator #(.width(3)) comparator_17 (.a(Instruction[14:12]), .b(3'b001), .eq(comparator_17_eq));  // open: gt, lt
  Comparator #(.width(3)) comparator_18 (.a(Instruction[14:12]), .b(3'b010), .eq(comparator_18_eq));  // open: gt, lt
  Comparator #(.width(3)) comparator_19 (.a(Instruction[14:12]), .b(3'b100), .eq(comparator_19_eq));  // open: gt, lt
  Comparator #(.width(3)) comparator_20 (.a(Instruction[14:12]), .b(3'b101), .eq(comparator_20_eq));  // open: gt, lt
  Comparator #(.width(3)) comparator_21 (.a(Instruction[14:12]), .b(3'b110), .eq(comparator_21_eq));  // open: gt, lt
  Comparator #(.width(3)) comparator_22 (.a(Instruction[14:12]), .b(3'b111), .eq(comparator_22_eq));  // open: gt, lt
  Comparator #(.width(3)) comparator_23 (.a(Instruction[14:12]), .b(3'b000), .eq(comparator_23_eq));  // open: gt, lt
  Comparator #(.width(3)) comparator_24 (.a(Instruction[14:12]), .b(3'b001), .eq(comparator_24_eq));  // open: gt, lt
  Comparator #(.width(3)) comparator_25 (.a(Instruction[14:12]), .b(3'b010), .eq(comparator_25_eq));  // open: gt, lt
  and and_16 (is_addi, comparator_15_eq, comparator_16_eq);
  and and_17 (is_slli, comparator_15_eq, comparator_17_eq);
  and and_18 (is_slti, comparator_15_eq, comparator_18_eq);
  and and_19 (is_xori, comparator_15_eq, comparator_19_eq);
  and and_20 (and_20_out, comparator_15_eq, comparator_20_eq);
  and and_21 (is_ori, comparator_15_eq, comparator_21_eq);
  and and_22 (is_andi, comparator_15_eq, comparator_22_eq);
  and and_23 (is_lb, comparator_14_eq, comparator_23_eq);
  and and_24 (is_lh, comparator_14_eq, comparator_24_eq);
  and and_25 (is_lw, comparator_14_eq, comparator_25_eq);
  Comparator #(.width(7)) comparator_26 (
    .a(Instruction[31:25]), .b({7{1'b0}}), .gt(comparator_26_gt), .eq(comparator_26_eq));  // open: lt
  and and_26 (is_srli, and_20_out, comparator_26_eq);
  and and_27 (is_srai, and_20_out, comparator_26_gt);
  Comparator #(.width(7)) comparator_27 (.a(Instruction[6:0]), .b(7'b0100011), .eq(comparator_27_eq));  // open: gt, lt
  Comparator #(.width(7)) comparator_28 (.a(Instruction[6:0]), .b(7'b1100011), .eq(comparator_28_eq));  // open: gt, lt
  Priority_Encoder #(.select_enc(6)) priority_encoder_1 (
    .in0(is_add), .in1(is_mul), .in2(is_sub), .in3(is_sll), .in4(is_mulh), .in5(is_mulhu), .in6(is_slt),
    .in7(is_xor), .in8(is_srl), .in9(is_sra), .in10(is_or), .in11(is_and), .in12(is_lb), .in13(is_lh),
    .in14(is_lw), .in15(is_addi), .in16(is_slli), .in17(is_slti), .in18(is_xori), .in19(is_srli),
    .in20(is_srai), .in21(is_ori), .in22(is_andi), .in23(is_sb), .in24(is_sh), .in25(is_sw), .in26(is_beq),
    .in27(is_bne), .in28(is_blt), .in29(is_bge), .in30(is_bltu), .in31(is_bgeu), .in32(is_auipc),
    .in33(is_lui), .in34(is_jal), .in35(is_jalr), .out(ROMInput));  // open: in36, in37, in38, in39, in40, in41, in42, in43, in44, in45, in46, in47, in48, in49, in50, in51, in52, in53, in54, in55, in56, in57, in58, in59, in60, in61, in62, in63, gs, en_out, en_in
  Comparator #(.width(3)) comparator_29 (.a(Instruction[14:12]), .b(3'b000), .eq(comparator_29_eq));  // open: gt, lt
  Comparator #(.width(3)) comparator_30 (.a(Instruction[14:12]), .b(3'b001), .eq(comparator_30_eq));  // open: gt, lt
  Comparator #(.width(3)) comparator_31 (.a(Instruction[14:12]), .b(3'b010), .eq(comparator_31_eq));  // open: gt, lt
  Comparator #(.width(3)) comparator_32 (.a(Instruction[14:12]), .b(3'b000), .eq(comparator_32_eq));  // open: gt, lt
  Comparator #(.width(3)) comparator_33 (.a(Instruction[14:12]), .b(3'b001), .eq(comparator_33_eq));  // open: gt, lt
  Comparator #(.width(3)) comparator_34 (.a(Instruction[14:12]), .b(3'b100), .eq(comparator_34_eq));  // open: gt, lt
  Comparator #(.width(3)) comparator_35 (.a(Instruction[14:12]), .b(3'b101), .eq(comparator_35_eq));  // open: gt, lt
  Comparator #(.width(3)) comparator_36 (.a(Instruction[14:12]), .b(3'b110), .eq(comparator_36_eq));  // open: gt, lt
  Comparator #(.width(3)) comparator_37 (.a(Instruction[14:12]), .b(3'b111), .eq(comparator_37_eq));  // open: gt, lt
  and and_28 (is_sb, comparator_27_eq, comparator_29_eq);
  and and_29 (is_sh, comparator_27_eq, comparator_30_eq);
  and and_30 (is_sw, comparator_27_eq, comparator_31_eq);
  and and_31 (is_beq, comparator_28_eq, comparator_32_eq);
  and and_32 (is_bne, comparator_28_eq, comparator_33_eq);
  and and_33 (is_blt, comparator_28_eq, comparator_34_eq);
  and and_34 (is_bge, comparator_28_eq, comparator_35_eq);
  and and_35 (is_bltu, comparator_28_eq, comparator_36_eq);
  and and_36 (is_bgeu, comparator_28_eq, comparator_37_eq);
  and and_37 (and_37_out, is_beq, BrEq);
  not not_1 (not_1_out, BrEq);
  and and_38 (and_38_out, is_blt, BrLt);
  not not_2 (not_2_out, BrLt);
  and and_39 (and_39_out, is_bltu, BrLt);
  and and_40 (and_40_out, is_bgeu, not_3_out);
  not not_3 (not_3_out, BrLt);
  and and_41 (and_41_out, is_bne, not_1_out);
  and and_42 (and_42_out, is_bge, not_2_out);
  or or_1 (PCSel, and_37_out, and_41_out, and_38_out, and_42_out, and_39_out, and_40_out, is_jal, is_jalr);
  Comparator #(.width(7)) comparator_38 (.a(Instruction[6:0]), .b(7'b0010111), .eq(is_auipc));  // open: gt, lt
  Comparator #(.width(7)) comparator_39 (.a(Instruction[6:0]), .b(7'b0110111), .eq(is_lui));  // open: gt, lt
  Comparator #(.width(7)) comparator_40 (.a(Instruction[6:0]), .b(7'b1101111), .eq(is_jal));  // open: gt, lt
  Comparator #(.width(7)) comparator_41 (.a(Instruction[6:0]), .b(7'b1100111), .eq(is_jalr));  // open: gt, lt

  // Other names for the same wires on the sheet: opcode[6:0] = Instruction[6:0]; func3[2:0] = Instruction[14:12];
  //   func7[6:0] = Instruction[31:25]

  // Notes on the sheet:
  //   INPUTS to your circuit
  //   Connect ROM Input here ->
  //   contents of rom_1 (hex, n*v repeats v):
  //   1001 1401 1601 1081 1481 1581 1101 1201 1281 1681 1301 1381 41 41 41 1041 10c1 1141 1241 12c1 16c1
  //   1341 13c1 842 8c2 942 4*1064 1074 1074 1067 17c7 2069 2041
  //   ROM FOR CONTROL LOGIC
  //   DON'T CHANGE THE LOCATIONS OF THE INPUTS AND OUTPUTS!
  //   This is only if you choose to do the ROM option
  //   CONNECT
  //   WIRE
  //   TO
  //   USE
  //   ROM
  //   OUTPUT from your circuit
  //   Reminder: If using ROM, use combinational logic for PCSel
endmodule
