// Logisim project partial-load.circ as structural Verilog: 1 circuit, main circuit partial_load
module partial_load (
  input  [31:0] Instruction,
  input  [31:0] MemAddress,
  input  [31:0] DataFromMem,
  output [31:0] DataToReg
);

  wire is_lb, is_lh, is_lw;
  wire [2:0] sel;
  wire [7:0] lbData, multiplexer_1_out;
  wire [15:0] lhData, multiplexer_2_out;
  wire [31:0] bit_extender_1_out, bit_extender_2_out, lwData;

  Multiplexer #(.select(2), .width(8)) multiplexer_1 (
    .in0(DataFromMem[7:0]), .in1(DataFromMem[15:8]), .in2(DataFromMem[23:16]), .in3(DataFromMem[31:24]),
    .out(multiplexer_1_out), .sel(MemAddress[1:0]));
  Multiplexer #(.select(2), .width(16)) multiplexer_2 (
    .in0(DataFromMem[15:0]), .in1(DataFromMem[23:8]), .in2(DataFromMem[31:16]), .out(multiplexer_2_out),
    .sel(MemAddress[1:0]));  // open: in3
  Multiplexer #(.select(3), .width(8)) multiplexer_3 (
    .in0(multiplexer_1_out), .out(lbData), .sel(Instruction[14:12]));  // open: in1, in2, in3, in4, in5, in6, in7
  Multiplexer #(.select(3), .width(16)) multiplexer_4 (
    .in1(multiplexer_2_out), .out(lhData), .sel(Instruction[14:12]));  // open: in0, in2, in3, in4, in5, in6, in7
  Multiplexer #(.select(3), .width(32)) multiplexer_5 (
    .in2(DataFromMem), .out(lwData), .sel(Instruction[14:12]));  // open: in0, in1, in3, in4, in5, in6, in7
  Comparator #(.mode("unsigned")) comparator_1 (.a(lbData), .b({8{1'b0}}), .gt(is_lb));  // open: eq, lt
  Comparator #(.mode("unsigned"), .width(16)) comparator_2 (.a(lhData), .b({16{1'b0}}), .gt(is_lh));  // open: eq, lt
  Comparator #(.mode("unsigned"), .width(32)) comparator_3 (.a(lwData), .b({32{1'b0}}), .gt(is_lw));  // open: eq, lt
  assign bit_extender_1_out = {{24{lbData[7]}}, lbData};  // Bit_Extender bit_extender_1
  assign bit_extender_2_out = {{16{lhData[15]}}, lhData};  // Bit_Extender bit_extender_2
  Priority_Encoder priority_encoder_1 (
    .in0(is_lb), .in1(is_lh), .in2(is_lw), .out(sel));  // open: in3, in4, in5, in6, in7, en_in, gs, en_out
  Multiplexer #(.select(3), .width(32)) multiplexer_6 (
    .in0(bit_extender_1_out), .in1(bit_extender_2_out), .in2(lwData), .out(DataToReg), .sel(sel));  // open: in3, in4, in5, in6, in7

  // Notes on the sheet:
  //   INPUTS to your circuit
  //   DON'T CHANGE THE LOCATIONS OF THE INPUTS AND OUTPUTS!
  //   OUTPUT from your circuit
endmodule
