// Logisim project partial-store.circ as structural Verilog: 1 circuit, main circuit partial_store
module partial_store (
  input  [31:0] Instruction,
  input  [31:0] MemAddress,
  input  [31:0] DataFromReg,
  input  MemWEn,
  output [3:0] MemWriteMask,
  output [31:0] DataToMem
);

  wire comparator_1_eq, w;
  wire [4:4] maskSel;
  wire [31:0] bit_extender_1_out, bit_extender_2_out, multiplexer_1_out, multiplexer_2_out, Result;

  not not_1 (maskSel[4], w);
  assign bit_extender_1_out = {{24{1'b0}}, DataFromReg[7:0]};  // Bit_Extender bit_extender_1
  assign bit_extender_2_out = {{16{1'b0}}, DataFromReg[15:0]};  // Bit_Extender bit_extender_2
  Multiplexer #(.select(2), .width(32)) multiplexer_1 (
    .in0(bit_extender_1_out), .in1({{16{1'b0}}, DataFromReg[7:0], {8{1'b0}}}),
    .in2({{8{1'b0}}, DataFromReg[7:0], {16{1'b0}}}), .in3({DataFromReg[7:0], {24{1'b0}}}),
    .out(multiplexer_1_out), .sel(MemAddress[1:0]));
  Multiplexer #(.select(2), .width(32)) multiplexer_2 (
    .in0(bit_extender_2_out), .in2({DataFromReg[15:0], {16{1'b0}}}), .out(multiplexer_2_out),
    .sel(MemAddress[1:0]));  // open: in1, in3
  Comparator #(.width(7)) comparator_1 (.a(Instruction[6:0]), .b(7'b0100011), .eq(comparator_1_eq));  // open: gt, lt
  Demultiplexer #(.width(32)) demultiplexer_1 (.out1(DataToMem), .in(Result), .sel(w));  // open: out0
  Multiplexer #(.select(3), .width(32)) multiplexer_3 (
    .in0(multiplexer_1_out), .in1(multiplexer_2_out), .in2(DataFromReg), .out(Result),
    .sel(Instruction[14:12]));  // open: in3, in4, in5, in6, in7
  and and_1 (w, comparator_1_eq, MemWEn);
  Multiplexer #(.select(5), .width(4)) multiplexer_4 (
    .in0(4'b0001), .in1(4'b0010), .in2(4'b0100), .in3(4'b1000), .in4(4'b0011), .in5(4'b0000), .in6(4'b1100),
    .in7(4'b0000), .in8(4'b1111), .in9(4'b0000), .in10(4'b0000), .in11(4'b0000), .in12(4'b0000),
    .in13(4'b0000), .in14(4'b0000), .in15(4'b0000), .in16(4'b0000), .in17(4'b0000), .in18(4'b0000),
    .in19(4'b0000), .in20(4'b0000), .in21(4'b0000), .in22(4'b0000), .in23(4'b0000), .in24(4'b0000),
    .in25(4'b0000), .in26(4'b0000), .in27(4'b0000), .in28(4'b0000), .in29(4'b0000), .in30(4'b0000),
    .in31(4'b0000), .out(MemWriteMask), .sel({maskSel[4], Instruction[13:12], MemAddress[1:0]}));

  // Other names for the same wires on the sheet: func3[2:0] = Instruction[14:12];
  //   maskSel[3:0] = {Instruction[13:12], MemAddress[1:0]}; sel[1:0] = MemAddress[1:0]

  // Notes on the sheet:
  //   INPUTS to your circuit
  //   DON'T CHANGE THE LOCATIONS OF THE INPUTS AND OUTPUTS!
  //   OUTPUT from your circuit
endmodule
